# Fritzing sketch schematic (saved by Fritzing 0.9.3b)
breadboards: 1

parts:
  Componente1 = Arduino Uno (Rev3)
  DS1 = DS18B20 1-Wire Temperature Sensor [part_number=DS18B20]
  Raspberry_Pi2 = Raspberry Pi 2
  Componente2 = RFID-RC522-v2
  R1 = Resistor [tolerance=±5% resistance=4.7k package="0603 [SMD]"]
  S2 = KY-026
  M1 = Dagu DGServo 9g (Top view) [part_number=RS001B]
  J1 = Piezo Speaker
  R2 = PHOTOCELL [package=photocell-kit]
  S3 = KY-026
  S4 = KY-026
  R3 = PHOTOCELL [package=photocell-kit]
  R4 = PHOTOCELL [package=photocell-kit]
  R5 = PHOTOCELL [package=photocell-kit]
  R6 = Resistor [tolerance=±5% resistance=3.9k package=THT]
  R7 = Resistor [tolerance=±5% resistance=3.9k package=THT]
  R8 = Resistor [tolerance=±5% resistance=3.9k package=THT]
  R12 = Resistor [tolerance=±5% resistance=3.9k package=THT]
  R11 = Rotary Potentiometer (Small) [maximum_resistance=100kΩ package=THT]  # not connected
  R14 = Rotary Potentiometer (Small) [maximum_resistance=100kΩ package=THT]  # not connected
  R10 = Rotary Potentiometer (Small) [maximum_resistance=100kΩ package=THT]  # not connected
  R13 = Rotary Potentiometer (Small) [maximum_resistance=100kΩ package=THT]  # not connected
  8_Channel_Relay1 = 8 Channel Power Relay

nets:
  N1: Componente1.A0, R4.P$2, R7.Pin_0
  N2: Componente1.A1, R3.P$2, R12.Pin_0
  N3: Componente1.A2, R5.P$2, R8.Pin_0
  N4: Componente1.A3, R2.P$2, R6.Pin_0
  N5: Componente1.D8, M1.pulse
  N6: Componente1.D9_PWM, Componente2.RST
  N7: Componente1.D10_PWM/SS, Componente2.SDA
  N8: Componente1.D11_PWM/MOSI, Componente2.MOSI
  N9: Componente1.D12/MISO, Componente2.MISO
  N10: Componente1.D13/SCK, Componente2.SCK
  GND: Componente1.GND, DS1.GND, Componente2.GND, M1.gnd, J1.pin1, S3.pin2, R6.Pin_1, R7.Pin_1, R8.Pin_1, R12.Pin_1
  N11: Componente1.D2, S3.pin4
  N12: Componente1.D3_PWM, S2.pin4
  N13: Componente1.D4, S4.pin4
  N14: Componente1.D5_PWM, DS1.DQ, R1.Pin_0
  N15: Componente1.D6_PWM, J1.pin2
  3V3: Componente1.3V3, Componente2.3.3V
  5V: Componente1.5V, DS1.VDD, R1.Pin_1, M1.vcc, R2.P$1, S3.pin3, R3.P$1, R4.P$1, R5.P$1
  N16: Raspberry_Pi2.GPIO21, 8_Channel_Relay1.IN8
  N17: Raspberry_Pi2.GPIO20, 8_Channel_Relay1.IN7
  N18: Raspberry_Pi2.GPIO16, 8_Channel_Relay1.IN6
  N19: Raspberry_Pi2.GPIO12, 8_Channel_Relay1.IN5
  N20: Raspberry_Pi2.GPIO25, 8_Channel_Relay1.IN4
  N21: Raspberry_Pi2.GPIO24, 8_Channel_Relay1.IN3
  N22: Raspberry_Pi2.GPIO23, 8_Channel_Relay1.IN2
  N23: Raspberry_Pi2.GPIO18, 8_Channel_Relay1.IN1
  GND_2: Raspberry_Pi2.GND, 8_Channel_Relay1.GND
  5V_2: Raspberry_Pi2.5V, 8_Channel_Relay1.VCC

notes:
  Laser point
  USB Serial to Rasp

custom parts:
  RFID-RC522-v2: A simple China made RFID-RC522 Reader; do check the pin labels, as this is a MFRC522 based clone.
  KY-026: ky-026 flame sensor module
  8 Channel Power Relay: An 8 channel power relay. The module operates at 5V.
